# Fritzing sketch Serial01_Ultrasonic (saved by Fritzing 1.0.2b)
breadboards: 1

parts:
  Teensy1 = Teensy 4.0
  HC-SR04_Sensor_1 = HC-SR04 Ultrasonic Distance Sensor

nets:
  N1: Teensy1.pin_1, Teensy1.pin_32, HC-SR04_Sensor_1.VCC
  N2: Teensy1.pin_11, HC-SR04_Sensor_1.TRIG
  N3: Teensy1.pin_12, HC-SR04_Sensor_1.ECHO
  N4: Teensy1.pin_31, HC-SR04_Sensor_1.GND

custom parts:
  Teensy 4.0: The Teensy is a complete USB-based microcontoller development system, in a very small footprint, capable of implementing many types of projects. All programming is done via the USB port. No special programmer is needed, only a standard micro-USB cable and a PC or Macintosh with a USB port.
